# Fritzing sketch V1-UseTimeCounter of tennis ball thrower (saved by Fritzing 0.9.3b)
breadboards: 1

parts:
  U1 = Voltage Regulator - 5V [package="TO220 [THT]"]
  U2 = LCD-16X2 [package=lcd-16x2]
  U3 = Voltage Regulator - 5V [package="TO220 [THT]"]
  Part1 = Arduino Uno (Rev3)
  BAT1 = 12 battery [package=battery]
  U4 = POT [package=trim_pot]
  Part3 = Voltage Sensor 25V
  IC1 = DS1302 [package="DIP8 [THT]"]
  R1 = Resistor [tolerance=±5% resistance=220 package="0603 [SMD]"]
  Thrower_On_Sends_5V_to_D8 = SWITCH-MOMENTARY-2 [package=tactile-switch-1101ne]

nets:
  N1: U1.input_voltage, BAT1.+, Part3.VCC, Part3.+, Thrower_On_Sends_5V_to_D8.1
  GND: U1.GND, U2.VSS, U3.GND, Part1.GND, BAT1.-, U4.S, Part3.GND, Part3.-, IC1.0V, R1.Pin_0
  VDD: U1.output_voltage, U2.VDD, U2.R_W, U2.A, Part1.VIN, U4.A, IC1.+V
  N2: U2.VO, U4.E
  N3: U2.RS, Part1.D2
  N4: U2.E, Part1.D3_PWM
  N5: U2.DB4, Part1.D4
  N6: U2.DB5, Part1.D5_PWM
  N7: U2.DB6, Part1.D6_PWM
  N8: U2.DB7, Part1.D7
  N9: U2.K, R1.Pin_1
  N10: U3.input_voltage, Thrower_On_Sends_5V_to_D8.2
  N11: U3.output_voltage, Part1.D8
  N12: Part1.A0, Part3.S
  N13: Part1.D9_PWM, IC1.SCLK_-_SPI_Clock
  N14: Part1.D10_PWM/SS, IC1.I/O_-_SPI_Data_In/Out
  N15: Part1.D11_PWM/MOSI, IC1.CE_-_Chip_Enable

custom parts:
  12 battery: 12V lead acid type battery, like the Husqvarna YTH2448 12V 35AH battery. This is the mini version 1/4 the size of the actual battery to be closer to typical breadboard parts (around 2in wide rathher than 7in). The pads in pcb are sized to accomidate up to 14ga wire (as these batterys will deliver high currents.)
